# Fritzing sketch ADS1115SunTracker (saved by Fritzing 0.9.10b)
circuit board: 4.41949cm x 3.85588cm
breadboards: 1

parts:
  Bottom_right = PHOTOCELL [package=photocell-kit]
  Top_right = PHOTOCELL [package=photocell-kit]
  ADS1115 = Adafruit ADS1115 16Bit I2C ADC [part_number="Adafruit #1085"]
  Top_left = PHOTOCELL [package=photocell-kit]
  Bottom_left = PHOTOCELL [package=photocell-kit]
  R6 = TRIMPOT [maximum_resistance=10kΩ knob_status=50% power=0.5W package=trim_pot_pth]
  R7 = TRIMPOT [maximum_resistance=10kΩ knob_status=50% power=0.5W package=trim_pot_pth]
  R5 = TRIMPOT [maximum_resistance=10kΩ knob_status=50% power=0.5W package=trim_pot_pth]
  R8 = TRIMPOT [maximum_resistance=10kΩ knob_status=50% power=0.5W package=trim_pot_pth]
  J1 = female pin header, 10 pins [form="♀ (female)"]
  J2 = male pin header, 4 pins [form="♂ (male)"]
  J3 = male pin header, 4 pins [form="♂ (male)"]

nets:
  5V: Bottom_right.P$1, Top_right.P$1, ADS1115.VDD, Top_left.P$1, Bottom_left.P$1, J1.pin1, J3.pin1
  Bottom right: Bottom_right.P$2, ADS1115.AIN3, R8.WIPER, J1.pin10
  Top right: Top_right.P$2, ADS1115.AIN1, R6.WIPER, J1.pin8
  Bottom left: ADS1115.AIN2, Bottom_left.P$2, R7.WIPER, J1.pin9
  Top left: ADS1115.AIN0, Top_left.P$2, R5.WIPER, J1.pin7
  alert: ADS1115.ALERT, J1.pin6
  addr: ADS1115.ADDR, J1.pin5, J2.pin1, J2.pin2, J2.pin3, J2.pin4
  sda: ADS1115.SDA, J1.pin4, J3.pin4
  scl: ADS1115.SCL, J1.pin3, J3.pin3
  GND: ADS1115.GND, R6.CW, R7.CW, R5.CW, R8.CW, J1.pin2, J3.pin2

notes:
  0x49
  0x48
  0x4B
  0x4A
  ©2023 Adam Howell

custom parts:
  Adafruit ADS1115 16Bit I2C ADC: For microcontrollers without an analog-to-digital converter or when you want a higher-precision ADC, the ADS1115 provides 16-bit precision at 860 samples/second over I2C. The chip can be configured as 4 single-ended input channels, or two differential channels. As a nice bonus, it even includes a programmable gain amplifier, up to x16, to help boost up smaller single/differential signals to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
